// Logisim project ALU-Datapath with fetch unit.circ as structural Verilog: 3 circuits, main circuit ALU_16bit
module ALU_16bit (
  input  [15:0] A,
  input  [15:0] B,
  input  [3:0] Shamt,
  input  [3:0] Opcode,
  output [15:0] Result
);

  wire comparator_1_eq, comparator_1_gt, comparator_1_lt;
  wire [15:0] adder_1_out, and_1_out, bit_extender_1_out, bit_extender_2_out, bit_extender_3_out,
       divider_1_out, divider_1_rem, multiplier_1_out, not_1_out, or_1_out, shifter_1_out, shifter_2_out,
       subtractor_1_out, xor_1_out;

  assign and_1_out = A & B;  // AND_Gate and_1, 16 bits wide
  assign or_1_out = A | B;  // OR_Gate or_1, 16 bits wide
  assign xor_1_out = A ^ B;  // XOR_Gate xor_1, 16 bits wide
  assign not_1_out = ~A;  // NOT_Gate not_1, 16 bits wide
  Adder #(.width(16)) adder_1 (.a(A), .b(B), .out(adder_1_out));  // open: cin, cout
  Subtractor #(.width(16)) subtractor_1 (.a(A), .b(B), .out(subtractor_1_out));  // open: bin, bout
  Multiplier #(.width(16)) multiplier_1 (.a(A), .b(B), .out(multiplier_1_out));  // open: cin, cout
  Divider #(.width(16)) divider_1 (.a(A), .b(B), .out(divider_1_out), .rem(divider_1_rem));  // open: upper
  Shifter #(.width(16)) shifter_1 (.in(A), .\dist (Shamt), .out(shifter_1_out));
  Shifter #(.shift("lr"), .width(16)) shifter_2 (.in(A), .\dist (Shamt), .out(shifter_2_out));
  Comparator #(.width(16)) comparator_1 (
    .a(A), .b(B), .gt(comparator_1_gt), .eq(comparator_1_eq), .lt(comparator_1_lt));
  assign bit_extender_1_out = {{15{1'b0}}, comparator_1_gt};  // Bit_Extender bit_extender_1
  assign bit_extender_2_out = {{15{1'b0}}, comparator_1_lt};  // Bit_Extender bit_extender_2
  assign bit_extender_3_out = {{15{1'b0}}, comparator_1_eq};  // Bit_Extender bit_extender_3
  Multiplexer #(.select(4), .width(16)) multiplexer_1 (
    .in0(and_1_out), .in1(or_1_out), .in2(xor_1_out), .in3(not_1_out), .in4(adder_1_out),
    .in5(subtractor_1_out), .in6(multiplier_1_out), .in7(divider_1_out), .in8(divider_1_rem),
    .in9(shifter_1_out), .in10(shifter_2_out), .in11(bit_extender_1_out), .in12(bit_extender_2_out),
    .in13(bit_extender_3_out), .out(Result), .sel(Opcode));  // open: in14, in15
endmodule

module Rtypedatapath (
  input  in_1
);

  wire button_1_out;
  wire [15:0] adder_1_out, alu_16bit_1_result, register_1_q, registerfile_16bit_1_readdata1,
       registerfile_16bit_1_readdata2;
  wire [19:0] rom_1_data;

  Register #(.width(16)) register_1 (.D(adder_1_out), .clk(button_1_out), .Q(register_1_q));  // open: en, clr
  ROM #(.addrWidth(16), .dataWidth(20)) rom_1 (.addr(register_1_q), .data(rom_1_data));
  Adder #(.width(16)) adder_1 (.a(16'h1), .b(register_1_q), .out(adder_1_out));  // open: cin, cout
  Button button_1 (.out(button_1_out));
  RegisterFile_16bit registerfile_16bit_1 (
    .Write(in_1), .WriteAddress(rom_1_data[7:4]), .Clock(button_1_out), .ReadAddress1(rom_1_data[15:12]),
    .ReadAddress2(rom_1_data[11:8]), .WriteData(alu_16bit_1_result),
    .ReadData1(registerfile_16bit_1_readdata1), .ReadData2(registerfile_16bit_1_readdata2));
  ALU_16bit alu_16bit_1 (
    .B(registerfile_16bit_1_readdata2), .A(registerfile_16bit_1_readdata1), .Shamt(rom_1_data[3:0]),
    .Opcode(rom_1_data[19:16]), .Result(alu_16bit_1_result));

  // Notes on the sheet:
  //   contents of rom_1 (hex, n*v repeats v):
  //   41230 71240 81250 55460 61270
  //   Shamt
  //   RD
  //   RT
  //   RS
  //   OPCOde
  //   ID:2157CSE00922
  //   Naimoon Jannat Prapti
  //   R-Type Datapath
endmodule

module RegisterFile_16bit (
  input  [15:0] WriteData,
  input  Write,
  input  [3:0] WriteAddress,
  input  Clock,
  input  [3:0] ReadAddress1,
  input  [3:0] ReadAddress2,
  output [15:0] ReadData1,
  output [15:0] ReadData2
);

  wire decoder_1_out0, decoder_1_out1, decoder_1_out2, decoder_1_out3, decoder_1_out4, decoder_1_out5,
       decoder_1_out6, decoder_1_out7, decoder_1_out8, decoder_1_out9, decoder_1_out10, decoder_1_out11,
       decoder_1_out12, decoder_1_out13, decoder_1_out14, decoder_1_out15;
  wire [15:0] R0_q, R1_q, R2_q, R3_q, R4_q, R5_q, R6_q, R7_q, R8_q, R9_q, R10_q, R11_q, R12_q, R13_q, R14_q,
       R15_q;

  Decoder #(.select(4)) decoder_1 (
    .out0(decoder_1_out0), .out1(decoder_1_out1), .out2(decoder_1_out2), .out3(decoder_1_out3),
    .out4(decoder_1_out4), .out5(decoder_1_out5), .out6(decoder_1_out6), .out7(decoder_1_out7),
    .out8(decoder_1_out8), .out9(decoder_1_out9), .out10(decoder_1_out10), .out11(decoder_1_out11),
    .out12(decoder_1_out12), .out13(decoder_1_out13), .out14(decoder_1_out14), .out15(decoder_1_out15),
    .sel(WriteAddress), .en(Write));
  Register #(.width(16)) R0 (.D(WriteData), .en(decoder_1_out0), .clk(Clock), .Q(R0_q));  // open: clr
  Register #(.width(16)) R1 (.D(WriteData), .en(decoder_1_out1), .clk(Clock), .Q(R1_q));  // open: clr
  Register #(.width(16)) R2 (.D(WriteData), .en(decoder_1_out2), .clk(Clock), .Q(R2_q));  // open: clr
  Register #(.width(16)) R3 (.D(WriteData), .en(decoder_1_out3), .clk(Clock), .Q(R3_q));  // open: clr
  Register #(.width(16)) R4 (.D(WriteData), .en(decoder_1_out4), .clk(Clock), .Q(R4_q));  // open: clr
  Register #(.width(16)) R5 (.D(WriteData), .en(decoder_1_out5), .clk(Clock), .Q(R5_q));  // open: clr
  Register #(.width(16)) R6 (.D(WriteData), .en(decoder_1_out6), .clk(Clock), .Q(R6_q));  // open: clr
  Register #(.width(16)) R7 (.D(WriteData), .en(decoder_1_out7), .clk(Clock), .Q(R7_q));  // open: clr
  Register #(.width(16)) R8 (.D(WriteData), .en(decoder_1_out8), .clk(Clock), .Q(R8_q));  // open: clr
  Register #(.width(16)) R9 (.D(WriteData), .en(decoder_1_out9), .clk(Clock), .Q(R9_q));  // open: clr
  Register #(.width(16)) R10 (.D(WriteData), .en(decoder_1_out10), .clk(Clock), .Q(R10_q));  // open: clr
  Register #(.width(16)) R11 (.D(WriteData), .en(decoder_1_out11), .clk(Clock), .Q(R11_q));  // open: clr
  Register #(.width(16)) R12 (.D(WriteData), .en(decoder_1_out12), .clk(Clock), .Q(R12_q));  // open: clr
  Register #(.width(16)) R13 (.D(WriteData), .en(decoder_1_out13), .clk(Clock), .Q(R13_q));  // open: clr
  Register #(.width(16)) R14 (.D(WriteData), .en(decoder_1_out14), .clk(Clock), .Q(R14_q));  // open: clr
  Register #(.width(16)) R15 (.D(WriteData), .en(decoder_1_out15), .clk(Clock), .Q(R15_q));  // open: clr
  Multiplexer #(.select(4), .width(16)) multiplexer_1 (
    .in0(R0_q), .in1(R1_q), .in2(R2_q), .in3(R3_q), .in4(R4_q), .in5(R5_q), .in6(R6_q), .in7(R7_q),
    .in8(R8_q), .in9(R9_q), .in10(R10_q), .in11(R11_q), .in12(R12_q), .in13(R13_q), .in14(R14_q),
    .in15(R15_q), .out(ReadData1), .sel(ReadAddress1));
  Multiplexer #(.select(4), .width(16)) multiplexer_2 (
    .in0(R0_q), .in1(R1_q), .in2(R2_q), .in3(R3_q), .in4(R4_q), .in5(R5_q), .in6(R6_q), .in7(R7_q),
    .in8(R8_q), .in9(R9_q), .in10(R10_q), .in11(R11_q), .in12(R12_q), .in13(R13_q), .in14(R14_q),
    .in15(R15_q), .out(ReadData2), .sel(ReadAddress2));
endmodule
